# Fritzing sketch ecg_project (saved by Fritzing 0.9.3b)
breadboards: 2

parts:
  S1 = Momentary Switch [package=tactile-pth]
  LED1 = smd LED [color="Green (555nm)" package="0805 [SMD]"]
  LED2 = smd LED [color="Yellow (585nm)" package="0805 [SMD]"]
  U3 = POT [package=pot_alpha_rv16af-20]
  U1 = ESP32-38PinWide [part_number=ESP32-38PinWide]
  U2 = POT [package=pot_alpha_rv16af-20]

nets:
  N1: S1.1, U1.GPIO15
  N2: S1.2, LED1.cathode, LED1.anode, LED2.cathode, LED2.anode, U3.E, U1.GPIO12, U1.GPIO13, U1.GPIO11, U2.E
  N3: U3.A, U1.3.3, U2.A
  N4: U3.S, U1.GPIO14
  N5: U1.GPIO4, U2.S

custom parts:
  ESP32-38PinWide: Generic 38-Pin ESP32 with wide format (only access to one side of pins on a breadboard) based on Stephen Lilley's HiLetgo ESP-WROOM-32 ESP32 ESP-32S Development Board.
