# Fritzing sketch wifiproject_board (saved by Fritzing 0.9.3b)
breadboards: 2

parts:
  U1 = ESP32-38PinWide [part_number=ESP32-38PinWide]
  DS1 = DS18B20 1-Wire Temperature Sensor [part_number=DS18B20]
  R1 = Resistor [tolerance=±5% resistance=4.7k package="1206 [SMD]"]
  sdCard1 = my_sdCard

nets:
  N1: U1.GPIO16, sdCard1.MISO
  N2: U1.GPIO5, sdCard1.CS
  N3: U1.GPIO18, sdCard1.SCK
  N4: U1.GPIO21, DS1.DQ, R1.Pin_0
  N5: U1.GPIO23, sdCard1.MOSI
  GND: DS1.GND, sdCard1.GND
  N6: DS1.VDD, R1.Pin_1

custom parts:
  ESP32-38PinWide: Generic 38-Pin ESP32 with wide format (only access to one side of pins on a breadboard) based on Stephen Lilley's HiLetgo ESP-WROOM-32 ESP32 ESP-32S Development Board.
  my_sdCard: micro sdCard Adapter with 90º pin header. Use a filtering Capacitor between CS and GND if needed. PCB View Pinouts are Reversed for laying parallel on PCB using a 90º pin header.
